# Fritzing sketch Rain_gauge_Mega_v1 (saved by Fritzing 0.9.3b)

parts:
  Part1 = Arduino Mega 2560 (Rev3)
  Part2 = Real Time Clock Module - DS1307 RTC Breakout Board
  Part3 = MicroSD Card Module
  S1 = Reed switch [package=THT]
  S2 = Reed switch [package=THT]
  S3 = Reed switch [package=THT]
  S4 = Reed switch [package=THT]
  S5 = Reed switch [package=THT]
  S6 = Reed switch [package=THT]
  S7 = Reed switch [package=THT]
  S8 = Reed switch [package=THT]
  S9 = Reed switch [package=THT]
  S10 = Reed switch [package=THT]
  S11 = Reed switch [package=THT]
  S12 = Reed switch [package=THT]
  S13 = Reed switch [package=THT]
  S14 = Reed switch [package=THT]
  S15 = Reed switch [package=THT]
  S16 = Reed switch [package=THT]
  S17 = Reed switch [package=THT]
  S18 = Reed switch [package=THT]
  S19 = Reed switch [package=THT]
  S20 = Reed switch [package=THT]
  R1 = Resistor [tolerance=±5% resistance=10k package="2512 [SMD]"]

nets:
  SCL: Part1.D21/SCL, Part1.SCL, Part2.SCL
  SDA: Part1.D20/SDA, Part1.SDA, Part2.SDA
  GND: Part1.GND, Part2.GND, Part3.GND, R1.Pin_0
  5V: Part1.5V, Part2.5V, Part3.VCC
  gauge_1: Part1.D22, S1.pin_2
  gauge_2: Part1.D23, S2.pin_2
  gauge_3: Part1.D24, S3.pin_2
  gauge_4: Part1.D25, S4.pin_2
  gauge_5: Part1.D26, S5.pin_2
  gauge_6: Part1.D27, S6.pin_2
  gauge_7: Part1.D28, S7.pin_2
  gauge_8: Part1.D29, S8.pin_2
  gauge_9: Part1.D30, S9.pin_2
  gauge_10: Part1.D31, S10.pin_2
  gauge_11: Part1.D32, S11.pin_2
  gauge_12: Part1.D33, S12.pin_2
  gauge_13: Part1.D34, S13.pin_2
  gauge_14: Part1.D35, S14.pin_2
  gauge_15: Part1.D36, S15.pin_2
  gauge_16: Part1.D37, S16.pin_2
  gauge_17: Part1.D38, S17.pin_2
  gauge_18: Part1.D39, S18.pin_2
  gauge_19: Part1.D40, S19.pin_2
  gauge_20: Part1.D41, S20.pin_2
  MISO: Part1.D50, Part3.MISO
  MOSI: Part1.D51, Part3.MOSI
  SCK: Part1.D52, Part3.SCK
  SS: Part1.D53, Part3.CS
  N1: S1.pin_1, S2.pin_1, S3.pin_1, S4.pin_1, S5.pin_1, S6.pin_1, S7.pin_1, S8.pin_1, S9.pin_1, S10.pin_1, S11.pin_1, S12.pin_1, S13.pin_1, S14.pin_1, S15.pin_1, S16.pin_1, S17.pin_1, S18.pin_1, S19.pin_1, S20.pin_1, R1.Pin_1
